// Digital circuit alu.dig as structural Verilog
module alu (
  input  [7:0] A,
  input  [7:0] B,
  input  [3:0] SELECT,
  output [7:0] S
);

  wire shiftleft_1_over, shiftright_1_over, somador8bits_1_overflow, subtrator8bits_1_overflow;
  wire [7:0] multiplicador4bits_1_produto, operadorand_1_and, operadoror_1_or, operadorxor_1_xor,
       shiftleft_1_left, shiftright_1_right, somador8bits_1_soma, \subtrator8bits_1_subtração ;

  operadorAND operadorand_1 (
    .B0(B[0]), .B1(B[1]), .B2(B[2]), .B3(B[3]), .B4(B[4]), .B5(B[5]), .B6(B[6]), .B7(B[7]), .A0(A[0]),
    .A1(A[1]), .A2(A[2]), .A3(A[3]), .A4(A[4]), .A5(A[5]), .A6(A[6]), .A7(A[7]), .AND(operadorand_1_and));
  operadorOR operadoror_1 (
    .B0(B[0]), .B1(B[1]), .B2(B[2]), .B3(B[3]), .B4(B[4]), .B5(B[5]), .B6(B[6]), .B7(B[7]), .A0(A[0]),
    .A1(A[1]), .A2(A[2]), .A3(A[3]), .A4(A[4]), .A5(A[5]), .A6(A[6]), .A7(A[7]), .OR(operadoror_1_or));
  operadorXOR operadorxor_1 (
    .B0(B[0]), .B1(B[1]), .B2(B[2]), .B3(B[3]), .B4(B[4]), .B5(B[5]), .B6(B[6]), .B7(B[7]), .A0(A[0]),
    .A1(A[1]), .A2(A[2]), .A3(A[3]), .A4(A[4]), .A5(A[5]), .A6(A[6]), .A7(A[7]), .XOR(operadorxor_1_xor));
  somador8bits somador8bits_1 (
    .A7(A[7]), .A6(A[6]), .A5(A[5]), .A4(A[4]), .A3(A[3]), .A2(A[2]), .A1(A[1]), .A0(A[0]), .B7(B[7]),
    .B6(B[6]), .B5(B[5]), .B4(B[4]), .B3(B[3]), .B2(B[2]), .B1(B[1]), .B0(B[0]),
    .OVERFLOW(somador8bits_1_overflow), .SOMA(somador8bits_1_soma));
  subtrator8bits subtrator8bits_1 (
    .A0(A[0]), .B0(B[0]), .A1(A[1]), .B1(B[1]), .A2(A[2]), .B2(B[2]), .A3(A[3]), .B3(B[3]), .A4(A[4]),
    .B4(B[4]), .A5(A[5]), .B5(B[5]), .A6(A[6]), .B6(B[6]), .A7(A[7]), .B7(B[7]),
    .\SUBTRAÇÃO (\subtrator8bits_1_subtração ), .OVERFLOW(subtrator8bits_1_overflow));
  multiplicador4bits multiplicador4bits_1 (
    .B0(B[0]), .B1(B[1]), .B2(B[2]), .A0(A[0]), .A1(A[1]), .A2(A[2]), .A3(A[3]), .B3(B[3]),
    .PRODUTO(multiplicador4bits_1_produto));
  shiftLeft shiftleft_1 (
    .A7(A[7]), .A6(A[6]), .A5(A[5]), .A4(A[4]), .A3(A[3]), .A2(A[2]), .A1(A[1]), .A0(A[0]),
    .OVER(shiftleft_1_over), .LEFT(shiftleft_1_left));
  shiftRight shiftright_1 (
    .A7(A[7]), .A6(A[6]), .A5(A[5]), .A4(A[4]), .A3(A[3]), .A2(A[2]), .A1(A[1]), .A0(A[0]),
    .RIGHT(shiftright_1_right), .OVER(shiftright_1_over));
  LED OVERFLOW (.in(somador8bits_1_overflow));
  LED OVERFLOW_2 (.in(subtrator8bits_1_overflow));
  LED OVERFLOW_3 (.in(shiftleft_1_over));
  LED OVERFLOW_4 (.in(shiftright_1_over));
  Multiplexer #(.Selector_Bits(4), .Bits(8)) multiplexer_1 (
    .sel(SELECT), .in_0(operadorand_1_and), .in_1(operadoror_1_or), .in_2(operadorxor_1_xor),
    .in_3(somador8bits_1_soma), .in_4(\subtrator8bits_1_subtração ), .in_5(multiplicador4bits_1_produto),
    .in_6(shiftleft_1_left), .in_7(shiftright_1_right), .in_8({8{1'b0}}), .in_9({8{1'b0}}),
    .in_10({8{1'b0}}), .in_11({8{1'b0}}), .in_12({8{1'b0}}), .in_13({8{1'b0}}), .in_14({8{1'b0}}),
    .in_15({8{1'b0}}), .out(S));
  Seven_Seg_Hex seven_seg_hex_1 (.d(S[3:0]), .dp(1'b0));
  Seven_Seg_Hex seven_seg_hex_2 (.d(A[3:0]), .dp(1'b0));
  Seven_Seg_Hex seven_seg_hex_3 (.d(B[3:0]), .dp(1'b0));

  // Notes on the sheet:
  //   Para selecionar uma operação, 
  //   considere os seguintes valores:
  //   0 - Operador AND
  //   1 - Operador OR
  //   2 - Operadpr XOR
  //   3 - Soma 8 bits
  //   4 - Subtração 8 bits
  //   5 - Multiplicação 4bits
  //   6 - Operador Shift Left
  //   7 - Operador Shift Right
  //   Valor do output
  //   Valor do input A
  //   Valor do input B
endmodule
