// Digital circuit cpu.dig as structural Verilog
module cpu (
  input  [3:0] PC
);

  wire Clock_out;
  wire [3:0] register_1_q, register_1_q_2;
  wire [7:0] alu_1_s;
  wire [11:0] eepromdualport_1_d;

  Button Clock (.out(Clock_out));
  EEPROMDualPort #(.AddrBits(4), .Bits(12)) eepromdualport_1 (
    .A(PC), .Din({12{1'b0}}), .str(1'b0), .C(Clock_out), .ld(1'b1), .D(eepromdualport_1_d));
  alu alu_1 (
    .A(eepromdualport_1_d[11:4]), .B({register_1_q_2, register_1_q}), .SELECT(eepromdualport_1_d[3:0]),
    .S(alu_1_s));
  Register #(.Bits(8)) register_1 (.D(alu_1_s), .C(Clock_out), .en(1'b1), .Q({register_1_q_2, register_1_q}));
  Seven_Seg_Hex seven_seg_hex_1 (.d(register_1_q_2), .dp(1'b0));
  Seven_Seg_Hex seven_seg_hex_2 (.d(register_1_q), .dp(1'b0));

  // Notes on the sheet:
  //   contents of eepromdualport_1 (hex, n*v repeats v):
  //   53,33,23,14
endmodule
