// Digital circuit multiplicador4bits.dig as structural Verilog
module multiplicador4bits (
  input  B0,
  input  B1,
  input  B2,
  input  A0,
  input  A1,
  input  A2,
  input  A3,
  input  B3,
  output [7:0] PRODUTO
);

  wire and_2_out, and_3_out, and_4_out, and_5_out, and_6_out, and_7_out, and_8_out, and_9_out, and_10_out,
       and_11_out, and_12_out, and_13_out, and_14_out, somador_1_p1, somador_1_p2, somador_1_p4,
       somador_2_p1, somador_2_p2, somador_2_p5, somador_3_p1, somador_3_p5, somador_4_p1, somador_5_p1,
       somador_5_p5, somador_6_p1, somador_7_p1, somador_7_p5, somador_8_p1, somador_8_p5, somador_10_p1,
       somador_10_p5, somador_12_p4;

  // somador somador_1: pin names not known; wires that end beside it: somador_1_p1, somador_1_p2, PRODUTO[7], somador_1_p4, PRODUTO[6]
  and and_1 (somador_1_p4, B3, A3);
  and and_2 (and_2_out, A3, B2);
  // somador somador_2: pin names not known; wires that end beside it: somador_2_p1, somador_2_p2, somador_1_p2, and_2_out, somador_2_p5
  and and_3 (and_3_out, B1, A3);
  // somador somador_3: pin names not known; wires that end beside it: somador_3_p1, and_3_out, somador_2_p2, 1'b0, somador_3_p5
  and and_4 (and_4_out, A2, B3);
  // somador somador_4: pin names not known; wires that end beside it: somador_4_p1, somador_2_p5, somador_1_p1, and_4_out, PRODUTO[5]
  and and_5 (and_5_out, A2, B2);
  // somador somador_5: pin names not known; wires that end beside it: somador_5_p1, somador_3_p5, somador_2_p1, and_5_out, somador_5_p5
  and and_6 (and_6_out, A1, B3);
  // somador somador_6: pin names not known; wires that end beside it: somador_6_p1, somador_5_p5, somador_4_p1, and_6_out, PRODUTO[4]
  and and_7 (and_7_out, B0, A3);
  and and_8 (and_8_out, B1, A2);
  // somador somador_7: pin names not known; wires that end beside it: somador_7_p1, and_8_out, somador_3_p1, and_7_out, somador_7_p5
  and and_9 (and_9_out, A1, B2);
  // somador somador_8: pin names not known; wires that end beside it: somador_8_p1, somador_7_p5, somador_5_p1, and_9_out, somador_8_p5
  and and_10 (and_10_out, A0, B3);
  // somador somador_9: pin names not known; wires that end beside it: 1'b0, somador_8_p5, somador_6_p1, and_10_out, PRODUTO[3], B3
  and and_11 (and_11_out, B0, A2);
  and and_12 (and_12_out, B1, A1);
  // somador somador_10: pin names not known; wires that end beside it: somador_10_p1, and_12_out, somador_7_p1, and_11_out, somador_10_p5
  and and_13 (and_13_out, A0, B2);
  // somador somador_11: pin names not known; wires that end beside it: 1'b0, somador_10_p5, somador_8_p1, and_13_out, PRODUTO[2], B2
  and and_14 (and_14_out, B1, A0);
  // somador somador_12: pin names not known; wires that end beside it: 1'b0, and_14_out, somador_10_p1, somador_12_p4, PRODUTO[1], B1
  and and_15 (somador_12_p4, B0, A1);
  and and_16 (PRODUTO[0], B0, A0);
endmodule
