// Digital circuit operadorOR.dig as structural Verilog
module operadorOR (
  input  B0,
  input  B1,
  input  B2,
  input  B3,
  input  B4,
  input  B5,
  input  B6,
  input  B7,
  input  A0,
  input  A1,
  input  A2,
  input  A3,
  input  A4,
  input  A5,
  input  A6,
  input  A7,
  output [7:0] OR
);

  or or_1 (OR[0], A0, B0);
  or or_2 (OR[1], A1, B1);
  or or_3 (OR[2], A2, B2);
  or or_4 (OR[3], A3, B3);
  or or_5 (OR[4], A4, B4);
  or or_6 (OR[5], A5, B5);
  or or_7 (OR[6], A6, B6);
  or or_8 (OR[7], A7, B7);
endmodule
