// Digital circuit shiftLeft.dig as structural Verilog
module shiftLeft (
  input  A7,
  input  A6,
  input  A5,
  input  A4,
  input  A3,
  input  A2,
  input  A1,
  input  A0,
  output OVER,
  output [7:0] LEFT
);


  assign LEFT = {A6, A5, A4, A3, A2, A1, A0, 1'b0};
  assign OVER = A7;
endmodule
