// Digital circuit shiftRight.dig as structural Verilog
module shiftRight (
  input  A7,
  input  A6,
  input  A5,
  input  A4,
  input  A3,
  input  A2,
  input  A1,
  input  A0,
  output [7:0] RIGHT,
  output OVER
);


  assign OVER = A0;
  assign RIGHT = {1'b0, A7, A6, A5, A4, A3, A2, A1};
endmodule
