// Digital circuit somador8bits.dig as structural Verilog
module somador8bits (
  input  A7,
  input  A6,
  input  A5,
  input  A4,
  input  A3,
  input  A2,
  input  A1,
  input  A0,
  input  B7,
  input  B6,
  input  B5,
  input  B4,
  input  B3,
  input  B2,
  input  B1,
  input  B0,
  output OVERFLOW,
  output [7:0] SOMA
);

  wire somador_1_p3, somador_2_p3, somador_3_p3, somador_4_p3, somador_5_p3, somador_6_p3, somador_7_p3;

  // somador somador_1: pin names not known; wires that end beside it: A7, B7, somador_1_p3, SOMA[7], OVERFLOW
  // somador somador_2: pin names not known; wires that end beside it: A6, B6, somador_2_p3, SOMA[6], somador_1_p3
  // somador somador_3: pin names not known; wires that end beside it: A5, B5, somador_3_p3, SOMA[5], somador_2_p3
  // somador somador_4: pin names not known; wires that end beside it: A4, B4, somador_4_p3, SOMA[4], somador_3_p3
  // somador somador_5: pin names not known; wires that end beside it: A3, B3, somador_5_p3, SOMA[3], somador_4_p3
  // somador somador_6: pin names not known; wires that end beside it: A2, B2, somador_6_p3, SOMA[2], somador_5_p3
  // somador somador_7: pin names not known; wires that end beside it: A1, B1, somador_7_p3, SOMA[1], somador_6_p3
  // somador somador_8: pin names not known; wires that end beside it: A0, B0, 1'b0, SOMA[0], somador_7_p3
endmodule
