// Digital circuit subtrator8bits.dig as structural Verilog
module subtrator8bits (
  input  A0,
  input  B0,
  input  A1,
  input  B1,
  input  A2,
  input  B2,
  input  A3,
  input  B3,
  input  A4,
  input  B4,
  input  A5,
  input  B5,
  input  A6,
  input  B6,
  input  A7,
  input  B7,
  output [7:0] \SUBTRAÇÃO ,
  output OVERFLOW
);

  wire not_1_out, not_2_out, not_3_out, not_4_out, not_5_out, not_6_out, not_7_out, not_8_out, somador_1_p1,
       somador_2_p1, somador_3_p1, somador_4_p1, somador_5_p1, somador_6_p1, somador_7_p1;

  not not_1 (not_1_out, B7);
  // somador somador_1: pin names not known; wires that end beside it: somador_1_p1, not_1_out, OVERFLOW, A7, \SUBTRAÇÃO [7]
  not not_2 (not_2_out, B6);
  // somador somador_2: pin names not known; wires that end beside it: somador_2_p1, not_2_out, somador_1_p1, A6, \SUBTRAÇÃO [6]
  not not_3 (not_3_out, B5);
  // somador somador_3: pin names not known; wires that end beside it: somador_3_p1, not_3_out, somador_2_p1, A5, \SUBTRAÇÃO [5]
  not not_4 (not_4_out, B4);
  // somador somador_4: pin names not known; wires that end beside it: somador_4_p1, not_4_out, somador_3_p1, A4, \SUBTRAÇÃO [4]
  not not_5 (not_5_out, B3);
  // somador somador_5: pin names not known; wires that end beside it: somador_5_p1, not_5_out, somador_4_p1, A3, \SUBTRAÇÃO [3]
  not not_6 (not_6_out, B2);
  // somador somador_6: pin names not known; wires that end beside it: somador_6_p1, not_6_out, somador_5_p1, A2, \SUBTRAÇÃO [2]
  not not_7 (not_7_out, B1);
  // somador somador_7: pin names not known; wires that end beside it: somador_7_p1, not_7_out, somador_6_p1, A1, \SUBTRAÇÃO [1]
  not not_8 (not_8_out, B0);
  // somador somador_8: pin names not known; wires that end beside it: 1'b1, not_8_out, somador_7_p1, A0, \SUBTRAÇÃO [0]
endmodule
